// Logisim project cpu.circ as structural Verilog: 5 circuits, main circuit ComputeProcessingUnit
module ComputeProcessingUnit (
);

  wire buffer_1_out, clock_1_out, comparator_1_eq, comparator_2_eq, comparator_3_eq, comparator_4_eq,
       comparator_5_eq, comparator_6_eq, comparator_7_eq, comparator_8_eq, comparator_9_eq, comparator_10_eq,
       controlled_buffer_15_out, controlled_buffer_18_out, not_1_out, or_1_out;
  wire [7:0] InstructionPointer_q, InstructionPointer_q_2, InstructionPointer_q_3, InstructionPointer_q_4,
       InstructionPointer_q_5, InstructionPointer_q_6, InstructionPointer_q_7, InstructionPointer_q_8;
  wire [15:0] controlled_buffer_12_out, ie_indextoselectorbits_1_selectorbits,
       ie_indextoselectorbits_2_selectorbits, not_2_out;
  wire [63:0] adder_1_out, adder_2_out, adder_3_out, controlled_buffer_1_out, controlled_buffer_6_out,
       controlled_buffer_8_out, controlled_buffer_10_out, controlled_buffer_11_out, divider_1_out,
       divider_1_rem, ie_getregister_1_data, ie_getregister_2_data, ie_getregister_3_data,
       ie_registergate_1_a_output, ie_registergate_1_b_output, ie_registergate_1_c_output,
       ie_registergate_1_d_output, ie_registergate_1_e_output, ie_registergate_1_f_output,
       ie_registergate_1_ip_output, InstructionCounter_q, multiplexer_1_out, multiplier_1_out, RegisterA_q,
       RegisterB_q, RegisterC_q, RegisterD_q, RegisterE_q, RegisterF_q, rom_1_p2, rom_1_p3, rom_1_p4,
       rom_1_p5, subtractor_1_out;

  Clock clock_1 (.out(clock_1_out));
  buf buffer_1 (buffer_1_out, clock_1_out);
  Adder #(.width(64)) adder_1 (.a(64'h1), .b(InstructionCounter_q), .out(adder_1_out));  // open: cin, cout
  Register #(.trigger("falling"), .width(64)) InstructionCounter (
    .D(adder_1_out), .en(buffer_1_out), .clk(clock_1_out), .Q(InstructionCounter_q));  // open: clr
  // Probe on InstructionCounter_q
  Multiplexer #(.width(64)) multiplexer_1 (
    .in0(adder_2_out), .in1(ie_registergate_1_ip_output), .out(multiplexer_1_out), .sel(not_1_out));
  not not_1 (not_1_out, comparator_1_eq);
  Register #(.width(64)) RegisterA (
    .D(ie_registergate_1_a_output), .en(clock_1_out), .clk(clock_1_out), .Q(RegisterA_q));  // open: clr
  Register #(.width(64)) RegisterB (
    .D(ie_registergate_1_b_output), .en(clock_1_out), .clk(clock_1_out), .Q(RegisterB_q));  // open: clr
  Register #(.width(64)) RegisterC (
    .D(ie_registergate_1_c_output), .en(clock_1_out), .clk(clock_1_out), .Q(RegisterC_q));  // open: clr
  Register #(.width(64)) RegisterD (
    .D(ie_registergate_1_d_output), .en(clock_1_out), .clk(clock_1_out), .Q(RegisterD_q));  // open: clr
  Register #(.width(64)) RegisterE (
    .D(ie_registergate_1_e_output), .en(clock_1_out), .clk(clock_1_out), .Q(RegisterE_q));  // open: clr
  Register #(.width(64)) RegisterF (
    .D(ie_registergate_1_f_output), .en(clock_1_out), .clk(clock_1_out), .Q(RegisterF_q));  // open: clr
  Register #(.width(64)) InstructionPointer (
    .D(multiplexer_1_out), .en(clock_1_out), .clk(clock_1_out),
    .Q({InstructionPointer_q_8, InstructionPointer_q_7, InstructionPointer_q_6, InstructionPointer_q_5, InstructionPointer_q_4, InstructionPointer_q_3, InstructionPointer_q_2, InstructionPointer_q}));  // open: clr
  // Probe on {InstructionPointer_q_8, InstructionPointer_q_7, InstructionPointer_q_6, InstructionPointer_q_5, InstructionPointer_q_4, InstructionPointer_q_3, InstructionPointer_q_2, InstructionPointer_q}
  Comparator #(.width(64)) comparator_1 (
    .a(ie_registergate_1_ip_output),
    .b({InstructionPointer_q_8, InstructionPointer_q_7, InstructionPointer_q_6, InstructionPointer_q_5, InstructionPointer_q_4, InstructionPointer_q_3, InstructionPointer_q_2, InstructionPointer_q}),
    .eq(comparator_1_eq));  // open: gt, lt
  Adder #(.width(64)) adder_2 (
    .a({InstructionPointer_q_8, InstructionPointer_q_7, InstructionPointer_q_6, InstructionPointer_q_5, InstructionPointer_q_4, InstructionPointer_q_3, InstructionPointer_q_2, InstructionPointer_q}),
    .b(64'h4), .out(adder_2_out));  // open: cin, cout
  // Probe on RegisterA_q
  // Probe on RegisterB_q
  // Probe on RegisterC_q
  // Probe on RegisterD_q
  // Probe on RegisterE_q
  // Probe on RegisterF_q
  // ROM #(.dataWidth(64), .line("quad")) rom_1: pin names not known; wires that end beside it: InstructionPointer_q, rom_1_p2, rom_1_p3, rom_1_p4, rom_1_p5
  // Probe on rom_1_p2
  // Probe on rom_1_p3
  // Probe on rom_1_p4
  // Probe on rom_1_p5
  Comparator #(.width(64)) comparator_2 (.a(rom_1_p2), .b(64'h7), .eq(comparator_2_eq));  // open: gt, lt
  Comparator #(.width(64)) comparator_3 (.a(rom_1_p2), .b(64'h8), .eq(comparator_3_eq));  // open: gt, lt
  IE_GetRegister ie_getregister_1 (
    .SelectRegister(rom_1_p3), .A(RegisterA_q), .B(RegisterB_q), .C(RegisterC_q), .D(RegisterD_q),
    .E(RegisterE_q), .F(RegisterF_q), .Data(ie_getregister_1_data));  // open: IP
  Comparator #(.width(64)) comparator_4 (.a(rom_1_p2), .b({64{1'b0}}), .eq(comparator_4_eq));  // open: gt, lt
  Comparator #(.width(64)) comparator_5 (.a(rom_1_p2), .b(64'h1), .eq(comparator_5_eq));  // open: gt, lt
  Comparator #(.width(64)) comparator_6 (.a(rom_1_p2), .b(64'h2), .eq(comparator_6_eq));  // open: gt, lt
  Comparator #(.width(64)) comparator_7 (.a(rom_1_p2), .b(64'h3), .eq(comparator_7_eq));  // open: gt, lt
  Comparator #(.width(64)) comparator_8 (.a(rom_1_p2), .b(64'h4), .eq(comparator_8_eq));  // open: gt, lt
  Comparator #(.width(64)) comparator_9 (.a(rom_1_p2), .b(64'h5), .eq(comparator_9_eq));  // open: gt, lt
  Comparator #(.width(64)) comparator_10 (.a(rom_1_p2), .b(64'h6), .eq(comparator_10_eq));  // open: gt, lt
  IE_GetRegister ie_getregister_2 (
    .SelectRegister(rom_1_p4), .A(RegisterA_q), .B(RegisterB_q), .C(RegisterC_q), .D(RegisterD_q),
    .E(RegisterE_q), .F(RegisterF_q), .Data(ie_getregister_2_data));  // open: IP
  Adder #(.width(64)) adder_3 (
    .a(ie_getregister_1_data), .b(ie_getregister_2_data), .out(adder_3_out));  // open: cin, cout
  Subtractor #(.width(64)) subtractor_1 (
    .a(ie_getregister_1_data), .b(ie_getregister_2_data), .out(subtractor_1_out));  // open: bin, bout
  Multiplier #(.width(64)) multiplier_1 (
    .a(ie_getregister_1_data), .b(ie_getregister_1_data), .out(multiplier_1_out));  // open: cin, cout
  Divider #(.width(64)) divider_1 (
    .a(ie_getregister_1_data), .b(ie_getregister_2_data), .out(divider_1_out), .rem(divider_1_rem));  // open: upper
  assign controlled_buffer_1_out = comparator_5_eq ? adder_3_out : 64'bz;  // Controlled_Buffer controlled_buffer_1
  assign controlled_buffer_1_out = comparator_6_eq ? subtractor_1_out : 64'bz;  // Controlled_Buffer controlled_buffer_2
  assign controlled_buffer_1_out = comparator_7_eq ? multiplier_1_out : 64'bz;  // Controlled_Buffer controlled_buffer_3
  assign controlled_buffer_1_out = comparator_8_eq ? divider_1_out : 64'bz;  // Controlled_Buffer controlled_buffer_4
  assign controlled_buffer_1_out = comparator_9_eq ? divider_1_rem : 64'bz;  // Controlled_Buffer controlled_buffer_5
  assign controlled_buffer_6_out = comparator_10_eq ? rom_1_p4 : 64'bz;  // Controlled_Buffer controlled_buffer_6
  or or_1 (or_1_out, comparator_5_eq, comparator_6_eq, comparator_7_eq, comparator_8_eq, comparator_9_eq);
  IE_RegisterGate ie_registergate_1 (
    .RegisterSelector(not_2_out), .A_Input(RegisterA_q), .B_Input(RegisterB_q), .C_Input(RegisterC_q),
    .D_Input(RegisterD_q), .E_Input(RegisterE_q), .F_Input(RegisterF_q),
    .IP_Input({InstructionPointer_q_8, InstructionPointer_q_7, InstructionPointer_q_6, InstructionPointer_q_5, InstructionPointer_q_4, InstructionPointer_q_3, InstructionPointer_q_2, InstructionPointer_q}),
    .A_Output(ie_registergate_1_a_output), .B_Output(ie_registergate_1_b_output),
    .C_Output(ie_registergate_1_c_output), .D_Output(ie_registergate_1_d_output),
    .E_Output(ie_registergate_1_e_output), .F_Output(ie_registergate_1_f_output),
    .IP_Output(ie_registergate_1_ip_output));
  IE_GetRegister ie_getregister_3 (
    .SelectRegister(rom_1_p5), .A(RegisterA_q), .B(RegisterB_q), .C(RegisterC_q), .D(RegisterD_q),
    .E(RegisterE_q), .F(RegisterF_q), .Data(ie_getregister_3_data));  // open: IP
  assign controlled_buffer_6_out = or_1_out ? controlled_buffer_1_out : 64'bz;  // Controlled_Buffer controlled_buffer_7
  assign controlled_buffer_8_out = or_1_out ? rom_1_p5 : 64'bz;  // Controlled_Buffer controlled_buffer_8
  assign controlled_buffer_8_out = comparator_10_eq ? rom_1_p3 : 64'bz;  // Controlled_Buffer controlled_buffer_9
  assign controlled_buffer_10_out = comparator_3_eq ? ie_getregister_1_data : 64'bz;  // Controlled_Buffer controlled_buffer_10
  assign not_2_out = ~controlled_buffer_12_out;  // NOT_Gate not_2, 16 bits wide
  assign controlled_buffer_11_out = comparator_3_eq ? rom_1_p4 : 64'bz;  // Controlled_Buffer controlled_buffer_11
  assign controlled_buffer_12_out = comparator_4_eq ? {16{1'b1}} : 16'bz;  // Controlled_Buffer controlled_buffer_12
  assign controlled_buffer_6_out = comparator_2_eq ? rom_1_p3 : 64'bz;  // Controlled_Buffer controlled_buffer_13
  assign controlled_buffer_8_out = comparator_2_eq ? 64'hf : 64'bz;  // Controlled_Buffer controlled_buffer_14
  assign controlled_buffer_15_out = or_1_out ? or_1_out : 1'bz;  // Controlled_Buffer controlled_buffer_15
  assign controlled_buffer_15_out = comparator_10_eq ? comparator_10_eq : 1'bz;  // Controlled_Buffer controlled_buffer_16
  assign controlled_buffer_15_out = comparator_2_eq ? comparator_2_eq : 1'bz;  // Controlled_Buffer controlled_buffer_17
  assign controlled_buffer_18_out = comparator_3_eq ? comparator_3_eq : 1'bz;  // Controlled_Buffer controlled_buffer_18
  IE_SetRegister ie_setregister_1 (
    .SelectRegister(controlled_buffer_8_out), .Enable(controlled_buffer_15_out),
    .Data(controlled_buffer_6_out), .RegisterA(ie_registergate_1_a_output),
    .RegisterB(ie_registergate_1_b_output), .RegisterC(ie_registergate_1_c_output),
    .RegisterD(ie_registergate_1_d_output), .RegisterE(ie_registergate_1_e_output),
    .RegisterF(ie_registergate_1_f_output), .RegisterIP(ie_registergate_1_ip_output));
  IE_SetRegister ie_setregister_2 (
    .SelectRegister(controlled_buffer_11_out), .Enable(controlled_buffer_18_out),
    .Data(controlled_buffer_10_out), .RegisterA(ie_registergate_1_a_output),
    .RegisterB(ie_registergate_1_b_output), .RegisterC(ie_registergate_1_c_output),
    .RegisterD(ie_registergate_1_d_output), .RegisterE(ie_registergate_1_e_output),
    .RegisterF(ie_registergate_1_f_output), .RegisterIP(ie_registergate_1_ip_output));
  IE_IndexToSelectorBits ie_indextoselectorbits_1 (
    .Enable(controlled_buffer_15_out), .RegisterIndex(controlled_buffer_8_out),
    .SelectorBits(ie_indextoselectorbits_1_selectorbits));
  IE_IndexToSelectorBits ie_indextoselectorbits_2 (
    .Enable(controlled_buffer_18_out), .RegisterIndex(controlled_buffer_11_out),
    .SelectorBits(ie_indextoselectorbits_2_selectorbits));
  assign controlled_buffer_12_out = ie_indextoselectorbits_1_selectorbits | ie_indextoselectorbits_2_selectorbits;  // OR_Gate or_2, 16 bits wide

  // Notes on the sheet:
  //   contents of rom_1 (hex, n*v repeats v):
  //   6 0 8 0 6 1 2 0 1 0 1 2 8 2 0 0 7 8
  //   NO_OP
  //   ADD
  //   SUB
  //   MUL
  //   DIV
  //   REM
  //   IMMEDIATE
  //   JUMP
  //   MOVE
  //   STORE
endmodule

module IE_SetRegister (
  input  [63:0] SelectRegister,
  input  Enable,
  input  [63:0] Data,
  output [63:0] RegisterA,
  output [63:0] RegisterB,
  output [63:0] RegisterC,
  output [63:0] RegisterD,
  output [63:0] RegisterE,
  output [63:0] RegisterF,
  output [63:0] RegisterIP
);

  wire demultiplexer_2_out0, demultiplexer_2_out1, demultiplexer_2_out2, demultiplexer_2_out3,
       demultiplexer_2_out4, demultiplexer_2_out5, demultiplexer_2_out15;
  wire [63:0] controlled_buffer_1_out, demultiplexer_1_out0, demultiplexer_1_out1, demultiplexer_1_out2,
       demultiplexer_1_out3, demultiplexer_1_out4, demultiplexer_1_out5, demultiplexer_1_out15;

  assign controlled_buffer_1_out = Enable ? Data : 64'bz;  // Controlled_Buffer controlled_buffer_1
  Demultiplexer #(.select(4), .width(64)) demultiplexer_1 (
    .out0(demultiplexer_1_out0), .out1(demultiplexer_1_out1), .out2(demultiplexer_1_out2),
    .out3(demultiplexer_1_out3), .out4(demultiplexer_1_out4), .out5(demultiplexer_1_out5),
    .out15(demultiplexer_1_out15), .in(controlled_buffer_1_out), .sel(SelectRegister[3:0]));  // open: out6, out7, out8, out9, out10, out11, out12, out13, out14
  Demultiplexer #(.select(4)) demultiplexer_2 (
    .out0(demultiplexer_2_out0), .out1(demultiplexer_2_out1), .out2(demultiplexer_2_out2),
    .out3(demultiplexer_2_out3), .out4(demultiplexer_2_out4), .out5(demultiplexer_2_out5),
    .out15(demultiplexer_2_out15), .in(Enable), .sel(SelectRegister[3:0]));  // open: out6, out7, out8, out9, out10, out11, out12, out13, out14
  assign RegisterD = demultiplexer_2_out3 ? demultiplexer_1_out3 : 64'bz;  // Controlled_Buffer controlled_buffer_2
  assign RegisterE = demultiplexer_2_out4 ? demultiplexer_1_out4 : 64'bz;  // Controlled_Buffer controlled_buffer_3
  assign RegisterF = demultiplexer_2_out5 ? demultiplexer_1_out5 : 64'bz;  // Controlled_Buffer controlled_buffer_4
  assign RegisterIP = demultiplexer_2_out15 ? demultiplexer_1_out15 : 64'bz;  // Controlled_Buffer controlled_buffer_5
  assign RegisterA = demultiplexer_2_out0 ? demultiplexer_1_out0 : 64'bz;  // Controlled_Buffer controlled_buffer_6
  assign RegisterB = demultiplexer_2_out1 ? demultiplexer_1_out1 : 64'bz;  // Controlled_Buffer controlled_buffer_7
  assign RegisterC = demultiplexer_2_out2 ? demultiplexer_1_out2 : 64'bz;  // Controlled_Buffer controlled_buffer_8
endmodule

module IE_GetRegister (
  input  [63:0] SelectRegister,
  input  [63:0] A,
  input  [63:0] B,
  input  [63:0] C,
  input  [63:0] D,
  input  [63:0] E,
  input  [63:0] F,
  input  [63:0] IP,
  output [63:0] Data
);

  Multiplexer #(.select(4), .width(64)) multiplexer_1 (
    .in0(A), .in1(B), .in2(C), .in3(D), .in4(E), .in5(F), .in15(IP), .out(Data), .sel(SelectRegister[3:0]));  // open: in6, in7, in8, in9, in10, in11, in12, in13, in14
endmodule

module IE_RegisterGate (
  input  [15:0] RegisterSelector,
  input  [63:0] A_Input,
  input  [63:0] B_Input,
  input  [63:0] C_Input,
  input  [63:0] D_Input,
  input  [63:0] E_Input,
  input  [63:0] F_Input,
  input  [63:0] IP_Input,
  output [63:0] A_Output,
  output [63:0] B_Output,
  output [63:0] C_Output,
  output [63:0] D_Output,
  output [63:0] E_Output,
  output [63:0] F_Output,
  output [63:0] IP_Output
);

  assign IP_Output = RegisterSelector[15] ? IP_Input : 64'bz;  // Controlled_Buffer controlled_buffer_1
  assign D_Output = RegisterSelector[3] ? D_Input : 64'bz;  // Controlled_Buffer controlled_buffer_2
  assign E_Output = RegisterSelector[4] ? E_Input : 64'bz;  // Controlled_Buffer controlled_buffer_3
  assign F_Output = RegisterSelector[5] ? F_Input : 64'bz;  // Controlled_Buffer controlled_buffer_4
  assign A_Output = RegisterSelector[0] ? A_Input : 64'bz;  // Controlled_Buffer controlled_buffer_5
  assign B_Output = RegisterSelector[1] ? B_Input : 64'bz;  // Controlled_Buffer controlled_buffer_6
  assign C_Output = RegisterSelector[2] ? C_Input : 64'bz;  // Controlled_Buffer controlled_buffer_7
endmodule

module IE_IndexToSelectorBits (
  input  Enable,
  input  [63:0] RegisterIndex,
  output [15:0] SelectorBits
);

  wire not_1_out;
  wire [15:0] multiplexer_1_out;

  Multiplexer #(.select(4), .width(16)) multiplexer_1 (
    .in0(16'h1), .in1(16'h2), .in2(16'h4), .in3(16'h8), .in4(16'h10), .in5(16'h20), .in6(16'h40),
    .in7(16'h80), .in8(16'h100), .in9(16'h200), .in10(16'h400), .in11({16{1'b0}}), .in12({16{1'b0}}),
    .in13({16{1'b0}}), .in14({16{1'b0}}), .in15(16'h8000), .out(multiplexer_1_out), .sel(RegisterIndex[3:0]));
  assign SelectorBits = Enable ? multiplexer_1_out : 16'bz;  // Controlled_Buffer controlled_buffer_1
  not not_1 (not_1_out, Enable);
  assign SelectorBits = not_1_out ? {16{1'b0}} : 16'bz;  // Controlled_Buffer controlled_buffer_2
endmodule
